# Fritzing sketch meta-stairs-schema (saved by Fritzing 1.0.5)
breadboards: 1

parts:
  Teensy1 = Teensy 4.1
  J6 = Basic Force Sensing Resistor (FSR) [package=THT]
  R4 = Resistor [tolerance=±5% resistance=10k package="0805 [SMD]"]
  R9 = Resistor [tolerance=±5% resistance=10k package="0805 [SMD]"]
  R10 = Resistor [tolerance=±5% resistance=10k package="0805 [SMD]"]
  R11 = Resistor [tolerance=±5% resistance=10k package="0805 [SMD]"]
  R12 = Resistor [tolerance=±5% resistance=10k package="0805 [SMD]"]
  R13 = Resistor [tolerance=±5% resistance=10k package="0805 [SMD]"]
  R14 = Resistor [tolerance=±5% resistance=10k package="0805 [SMD]"]
  R15 = Resistor [tolerance=±5% resistance=10k package="0805 [SMD]"]
  R16 = Resistor [tolerance=±5% resistance=10k package="0805 [SMD]"]
  J7 = Basic Force Sensing Resistor (FSR) [package=THT]
  J8 = Basic Force Sensing Resistor (FSR) [package=THT]
  J9 = Basic Force Sensing Resistor (FSR) [package=THT]
  J10 = Basic Force Sensing Resistor (FSR) [package=THT]
  J11 = Basic Force Sensing Resistor (FSR) [package=THT]
  J12 = Basic Force Sensing Resistor (FSR) [package=THT]
  J13 = Basic Force Sensing Resistor (FSR) [package=THT]
  J14 = Basic Force Sensing Resistor (FSR) [package=THT]

nets:
  N1: Teensy1.D9, Teensy1.D13, Teensy1.A13/D27
  N2: Teensy1.D10, Teensy1.A1/D15
  N3: Teensy1.GND2#31, Teensy1.A15/D39, R4.Pin_0, R9.Pin_0, R10.Pin_0, R11.Pin_0, R12.Pin_0, R13.Pin_0, R14.Pin_0, R15.Pin_0, R16.Pin_0
  N4: Teensy1.A11/D25, Teensy1.A12/D26
  N5: Teensy1.D33, R11.Pin_1, J10.pin_1
  N6: J6.pin_0, J7.pin_0, J8.pin_0, J9.pin_0, J10.pin_0, J11.pin_0, J12.pin_0, J13.pin_0, J14.pin_0
  N7: J6.pin_1, R15.Pin_1
  N8: R4.Pin_1, J13.pin_1
  N9: R9.Pin_1, J12.pin_1
  N10: R10.Pin_1, J11.pin_1
  N11: R12.Pin_1, J9.pin_1
  N12: R13.Pin_1, J8.pin_1
  N13: R14.Pin_1, J7.pin_1
  N14: R16.Pin_1, J14.pin_1

custom parts:
  Teensy 4.1: The Teensy is a complete USB-based microcontoller development system, in a very small footprint, capable of implementing many types of projects. All programming is done via the USB port. No special programmer is needed, only a standard micro-USB cable and a PC or Macintosh with a USB port.
